// Logisim project processador.circ as structural Verilog: 3 circuits, main circuit main
module main (
  input  in_1,
  output [7:0] out_2
);

  wire clock_1_out;
  wire [7:0] adder_1_out, PC_q;

  Register PC (.D(adder_1_out), .Q(PC_q), .clk(clock_1_out), .clr(in_1));  // open: en
  Clock clock_1 (.out(clock_1_out));
  Adder adder_1 (.a(8'h1), .b(PC_q), .out(adder_1_out));  // open: cin, cout
  ROM rom_1 (.addr(PC_q));  // open: data, sel
  registradores Registradores ();  // open: Read_reg_1, Read_reg_2, Write_data, Write_reg, RegWrite, CLOCK, CLEAR, Read_data_1, Read_data_2

  // Notes on the sheet:
  //   contents of rom_1 (hex, n*v repeats v):
  //   1 ff 3 8
endmodule

module registradores (
  input  [2:0] Read_reg_1,
  input  [2:0] Read_reg_2,
  input  [7:0] Write_data,
  input  [2:0] Write_reg,
  input  RegWrite,
  input  CLOCK,
  input  CLEAR,
  output [7:0] Read_data_1,
  output [7:0] Read_data_2
);

  wire WE0, WE1, WE2, WE3, WE4, WE5, WE6, WE7;
  wire [7:0] demultiplexer_2_out0, demultiplexer_2_out1, demultiplexer_2_out2, demultiplexer_2_out3,
       demultiplexer_2_out4, demultiplexer_2_out5, demultiplexer_2_out6, demultiplexer_2_out7, Reg0, Reg1,
       Reg2, Reg3, Reg4, Reg5, Reg6, Reg7;

  Demultiplexer #(.select(3), .enable("false")) demultiplexer_1 (
    .out0(WE0), .out1(WE1), .out2(WE2), .out3(WE3), .out4(WE4), .out5(WE5), .out6(WE6), .out7(WE7),
    .in(RegWrite), .sel(Write_reg));
  Demultiplexer #(.select(3), .width(8), .enable("false")) demultiplexer_2 (
    .out0(demultiplexer_2_out0), .out1(demultiplexer_2_out1), .out2(demultiplexer_2_out2),
    .out3(demultiplexer_2_out3), .out4(demultiplexer_2_out4), .out5(demultiplexer_2_out5),
    .out6(demultiplexer_2_out6), .out7(demultiplexer_2_out7), .in(Write_data), .sel(Write_reg));
  Register Reg_0 (.D(demultiplexer_2_out0), .en(WE0), .Q(Reg0), .clk(CLOCK), .clr(CLEAR));
  Register Reg_1 (.D(demultiplexer_2_out1), .en(WE1), .Q(Reg1), .clk(CLOCK), .clr(CLEAR));
  Register Reg_2 (.D(demultiplexer_2_out2), .en(WE2), .Q(Reg2), .clk(CLOCK), .clr(CLEAR));
  Register Reg_3 (.D(demultiplexer_2_out3), .en(WE3), .Q(Reg3), .clk(CLOCK), .clr(CLEAR));
  Register Reg_4 (.D(demultiplexer_2_out4), .en(WE4), .Q(Reg4), .clk(CLOCK), .clr(CLEAR));
  Register Reg_5 (.D(demultiplexer_2_out5), .en(WE5), .Q(Reg5), .clk(CLOCK), .clr(CLEAR));
  Register Reg_6 (.D(demultiplexer_2_out6), .en(WE6), .Q(Reg6), .clk(CLOCK), .clr(CLEAR));
  Register Reg_7 (.D(demultiplexer_2_out7), .en(WE7), .Q(Reg7), .clk(CLOCK), .clr(CLEAR));
  Multiplexer #(.select(3), .width(8), .enable("false")) multiplexer_1 (
    .in0(Reg0), .in1(Reg1), .in2(Reg2), .in3(Reg3), .in4(Reg4), .in5(Reg5), .in6(Reg6), .in7(Reg7),
    .out(Read_data_1), .sel(Read_reg_1));
  Multiplexer #(.select(3), .width(8), .enable("false")) multiplexer_2 (
    .in0(Reg0), .in1(Reg1), .in2(Reg2), .in3(Reg3), .in4(Reg4), .in5(Reg5), .in6(Reg6), .in7(Reg7),
    .out(Read_data_2), .sel(Read_reg_2));

  // Other names for the same wires on the sheet: Read1[2:0] = Read_reg_1; Read2[2:0] = Read_reg_2
endmodule

module ULA (
  input  [7:0] A,
  input  [7:0] B,
  input  [2:0] \Função ,
  input  [2:0] Shamt,
  output [7:0] R,
  output Igual
);

  wire [7:0] AComp, ADiv, AMult, ANeg, AShiftDir, AShiftEsq, ASoma, ASub, BComp, BDiv, BMult, BSoma, BSub;

  Demultiplexer #(.select(3), .width(8), .enable("false")) demultiplexer_1 (
    .out0(ASoma), .out1(ASub), .out2(AMult), .out3(ADiv), .out4(ANeg), .out5(AComp), .out6(AShiftEsq),
    .out7(AShiftDir), .in(A), .sel(\Função ));
  Demultiplexer #(.select(3), .width(8), .enable("false")) demultiplexer_2 (
    .out0(BSoma), .out1(BSub), .out2(BMult), .out3(BDiv), .out5(BComp), .in(B), .sel(\Função ));  // open: out4, out6, out7
  Adder adder_1 (.a(ASoma), .b(BSoma));  // open: out, cin, cout
  Subtractor subtractor_1 (.a(ASub), .b(BSub));  // open: out, bin, bout
  Multiplier multiplier_1 (.a(AMult), .b(BMult));  // open: out, cin, cout
  Divider divider_1 (.a(ADiv), .b(BDiv));  // open: out, upper, rem
  Negator negator_1 (.in(ANeg));  // open: out
  Comparator comparator_1 (.a(AComp), .b(BComp));  // open: gt, eq, lt
  Shifter shifter_1 (.in(AShiftEsq), .\dist (Shamt));  // open: out
  Shifter #(.shift("lr")) shifter_2 (.in(AShiftDir), .\dist (Shamt));  // open: out
  Multiplexer #(.select(3), .enable("false")) multiplexer_1 ();  // open: in0, in1, in2, in3, in4, in5, in6, in7, out, sel
endmodule
